# Fritzing sketch distance_sensor (saved by Fritzing 0.9.2b)
breadboards: 1

parts:
  パーツ1 = SRF05 Ultrasonic Rangefinder
  パーツ2 = Arduino Uno (Rev3)

nets:
  VCC: パーツ1.VCC, パーツ2.5V
  N1: パーツ1.Trig, パーツ2.D2
  N2: パーツ1.Echo, パーツ2.D3_PWM
  GND: パーツ1.GND, パーツ2.GND
